# Fritzing sketch KompletteSchaltung (saved by Fritzing 0.9.3b)
breadboards: 1

parts:
  Bauteil1 = Arduino Nano (Rev3.0)
  J1 = Piezo Speaker
  M1 = DC Motor
  M2 = DC Motor
  hc-sr1 = hc-sr04
  hc-sr2 = hc-sr04
  Bauteil2 = Bluetooth HC-05 Macho
  S1 = H-Bridge with L298N
  VCC1 = Battery

nets:
  N1: Bauteil1.D1/TX, Bauteil2.RXD
  N2: Bauteil1.D0/RX, Bauteil2.TXD
  GND: Bauteil1.GND, J1.pin1, hc-sr1.GND, hc-sr2.GND, Bauteil2.GND, S1.GND, VCC1.-
  N3: Bauteil1.D2, hc-sr2.Echo
  N4: Bauteil1.D3, J1.pin2
  N5: Bauteil1.D4, S1.IN4
  N6: Bauteil1.D5, S1.IN3
  N7: Bauteil1.D6, S1.ENB
  N8: Bauteil1.D7, S1.IN1
  N9: Bauteil1.D8, hc-sr2.Trig
  N10: Bauteil1.D9, S1.ENA
  N11: Bauteil1.D10, S1.IN2
  N12: Bauteil1.D11/MOSI, hc-sr1.Echo
  N13: Bauteil1.D12/MISO, hc-sr1.Trig
  VIN: Bauteil1.VIN, S1.12V, VCC1.+
  VCC: Bauteil1.5V, hc-sr1.VCC, hc-sr2.VCC, Bauteil2.VCC
  N14: M1.pin_1, S1.M2-02
  N15: M1.pin_2, S1.M2-01
  N16: M2.pin_1, S1.M1-02
  N17: M2.pin_2, S1.M1-01

custom parts:
  H-Bridge with L298N: h-bridge
